# Fritzing sketch Resistenza_digitale (saved by Fritzing 0.9.3b)
breadboards: 1

parts:
  IC2 = Dual digital potentiometer [package=dil-08]
  IC3 = Dual digital potentiometer [package=dil-08]

nets:
  N1: IC2.SCK, IC3.SCK
  N2: IC2.SI, IC3.SI
  VSS: IC2.VSS, IC3.VSS
  N3: IC2.PW0, IC3.PW0
  N4: IC2.PB0, IC3.PB0
  N5: IC2.VDD+, IC3.VDD+

notes:
  Code at
  https://github.com/davidecaminati/ArduinoParallelResistorsMCP41010
  2
  Keypad version1
  Use Arduino UNO
  1
  Equivalent Resistor PINS
